# Fritzing sketch wiring (saved by Fritzing 0.9.2b)
breadboards: 1

parts:
  Teensy_3_1 = Teensy 3.1
  U1 = MMA7361 [package=lga14]

nets:
  N1: Teensy_3_1.D12, U1.SLEEP
  N2: Teensy_3_1.A1/D15, U1.XOUT
  N3: Teensy_3_1.A2/D16, U1.YOUT
  3V3: Teensy_3_1.3V3, U1.VSS
  N4: Teensy_3_1.AGND, U1.0GD

notes:
  MMA7361 Accelerometer
  14 = X
  15 = Y
  16 = Z
  12 = Sleep
  3.3V
